// Logisim project dc-10-205713B.circ as structural Verilog
// FA
module FULL_ADDER (
  input  A,
  input  B,
  input  Ci,
  output S,
  output Co
);

  wire and_1_out, and_2_out, and_3_out;

  or or_1 (Co, and_1_out, and_2_out, and_3_out);
  xor xor_1 (S, A, B, Ci);
  and and_1 (and_1_out, A, B);
  and and_2 (and_2_out, B, Ci);
  and and_3 (and_3_out, A, Ci);
endmodule

module _4BIT_ADDER (
  input  [3:0] A_3_0,
  input  [3:0] B_3_0,
  output [4:0] Y_4_0
);

  wire full_adder_2_co, full_adder_3_co, half_adder1_1_c;

  FULL_ADDER full_adder_1 (.S(Y_4_0[3]), .Co(Y_4_0[4]), .A(A_3_0[3]), .B(B_3_0[3]), .Ci(full_adder_2_co));
  FULL_ADDER full_adder_2 (.S(Y_4_0[2]), .Co(full_adder_2_co), .A(A_3_0[2]), .B(B_3_0[2]), .Ci(full_adder_3_co));
  FULL_ADDER full_adder_3 (.S(Y_4_0[1]), .Co(full_adder_3_co), .A(A_3_0[1]), .B(B_3_0[1]), .Ci(half_adder1_1_c));
  HALF_ADDER1 half_adder1_1 (.S(Y_4_0[0]), .C(half_adder1_1_c), .A(A_3_0[0]), .B(B_3_0[0]));
endmodule

// HA
module HALF_ADDER1 (
  input  A,
  input  B,
  output S,
  output C
);

  xor xor_1 (S, A, B);
  and and_1 (C, B, A);
endmodule

module HALF_SUBTRUCTOR (
  input  A,
  input  B,
  output BR,
  output D
);

  wire and_2_out, and_3_out, not_1_out, not_2_out, not_3_out;

  not not_1 (not_1_out, A);
  and and_1 (BR, not_1_out, B);
  not not_2 (not_2_out, A);
  and and_2 (and_2_out, not_2_out, B);
  and and_3 (and_3_out, A, not_3_out);
  not not_3 (not_3_out, B);
  or or_1 (D, and_2_out, and_3_out);
endmodule

module FULL_SUBTRUCTOR (
  input  A,
  input  B,
  input  BRi,
  output BRo,
  output D
);

  wire and_1_out, and_2_out, and_3_out, and_4_out, and_5_out, and_6_out, and_7_out, not_1_out, not_2_out,
       not_3_out, not_4_out, not_5_out, not_6_out, not_7_out, not_8_out;

  not not_1 (not_1_out, A);
  and and_1 (and_1_out, not_1_out, BRi);
  not not_2 (not_2_out, A);
  and and_2 (and_2_out, not_2_out, B);
  and and_3 (and_3_out, B, BRi);
  not not_3 (not_3_out, A);
  and and_4 (and_4_out, not_3_out, not_4_out, BRi);
  not not_4 (not_4_out, B);
  not not_5 (not_5_out, A);
  and and_5 (and_5_out, not_5_out, B, not_6_out);
  not not_6 (not_6_out, BRi);
  and and_6 (and_6_out, A, not_7_out, not_8_out);
  not not_7 (not_7_out, B);
  not not_8 (not_8_out, BRi);
  and and_7 (and_7_out, BRi, A, B);
  or or_1 (BRo, and_1_out, and_2_out, and_3_out);
  or or_2 (D, and_4_out, and_5_out, and_6_out, and_7_out);
endmodule

// SUB
module _4BET_SUBTRUCTOR (
  input  [3:0] A_3_0,
  input  [3:0] B_3_0,
  output [4:0] Y_4_0
);

  wire full_subtructor_1_p5, full_subtructor_2_p5, full_subtructor_3_p5;

  // FULL_SUBTRUCTOR full_subtructor_1: pin names not known; wires that end beside it: Y_4_0[3], Y_4_0[4], A_3_0[3], B_3_0[3], full_subtructor_1_p5
  // FULL_SUBTRUCTOR full_subtructor_2: pin names not known; wires that end beside it: Y_4_0[2], full_subtructor_1_p5, A_3_0[2], B_3_0[2], full_subtructor_2_p5
  // FULL_SUBTRUCTOR full_subtructor_3: pin names not known; wires that end beside it: Y_4_0[1], full_subtructor_2_p5, A_3_0[1], B_3_0[1], full_subtructor_3_p5
  HALF_SUBTRUCTOR half_subtructor_1 (.A(Y_4_0[0]), .B(full_subtructor_3_p5), .BR(A_3_0[0]), .D(B_3_0[0]));
endmodule

module NOT (
  input  [3:0] A_3_0,
  input  in_2,
  output [4:0] Y_4_0
);

  not not_1 (Y_4_0[3], A_3_0[3]);
  not not_2 (Y_4_0[2], A_3_0[2]);
  not not_3 (Y_4_0[1], A_3_0[1]);
  not not_4 (Y_4_0[0], A_3_0[0]);

  assign Y_4_0[4] = in_2;
endmodule

module AND (
  input  [3:0] in_1,
  input  [3:0] in_2,
  input  in_3,
  output [4:0] Y_4_0
);

  and and_1 (Y_4_0[2], in_1[2], in_2[2]);
  and and_2 (Y_4_0[3], in_1[3], in_2[3]);
  and and_3 (Y_4_0[1], in_1[1], in_2[1]);
  and and_4 (Y_4_0[0], in_1[0], in_2[0]);

  assign Y_4_0[4] = in_3;
endmodule

module OR (
  input  [3:0] in_1,
  input  [3:0] in_2,
  input  in_3,
  output [4:0] Y_4_0
);

  or or_1 (Y_4_0[2], in_1[2], in_2[2]);
  or or_2 (Y_4_0[3], in_1[3], in_2[3]);
  or or_3 (Y_4_0[1], in_1[1], in_2[1]);
  or or_4 (Y_4_0[0], in_1[0], in_2[0]);

  assign Y_4_0[4] = in_3;
endmodule

module XOR (
  input  [3:0] in_1,
  input  [3:0] in_2,
  input  in_3,
  output [4:0] Y_4_0
);

  xor xor_1 (Y_4_0[3], in_1[3], in_2[3]);
  xor xor_2 (Y_4_0[2], in_1[2], in_2[2]);
  xor xor_3 (Y_4_0[0], in_1[0], in_2[0]);
  xor xor_4 (Y_4_0[1], in_1[1], in_2[1]);

  assign Y_4_0[4] = in_3;
endmodule

module LS (
  input  [3:0] A_3_0,
  input  in_2,
  output [4:0] Y_4_0
);


  assign Y_4_0 = {A_3_0, in_2};
endmodule

module RS (
  input  [3:0] A_3_0,
  input  in_2,
  output [4:0] Y_4_0
);


  assign Y_4_0 = {A_3_0[0], in_2, A_3_0[3:1]};
endmodule

module AUX (
  input  [3:0] A_3_0,
  input  [3:0] B_3_0,
  input  [2:0] OP_2_0,
  output [4:0] Y_4_0
);

  wire [4:0] and_1_p3, n4bet_subtructor_1_y_4_0, n4bit_adder_1_y_4_0, not_1_y_4_0, or_1_p3, undriven,
       undriven_2, xor_1_p3;

  _4BIT_ADDER u_4bit_adder_1 (.A_3_0(A_3_0), .B_3_0(B_3_0), .Y_4_0(n4bit_adder_1_y_4_0));
  _4BET_SUBTRUCTOR u_4bet_subtructor_1 (.A_3_0(A_3_0), .B_3_0(B_3_0), .Y_4_0(n4bet_subtructor_1_y_4_0));
  NOT not_1 (.A_3_0(A_3_0), .in_2(B_3_0[0]), .Y_4_0(not_1_y_4_0));
  // AND and_1: pin names not known; wires that end beside it: A_3_0, B_3_0, and_1_p3
  // OR or_1: pin names not known; wires that end beside it: A_3_0, B_3_0, or_1_p3
  // XOR xor_1: pin names not known; wires that end beside it: A_3_0, B_3_0, xor_1_p3
  LS ls_1 (.A_3_0(A_3_0), .in_2(undriven[0]));  // open: Y_4_0
  RS rs_1 (.A_3_0(A_3_0), .in_2(undriven_2[0]));  // open: Y_4_0
  Multiplexer #(.select(3), .width(5)) multiplexer_1 (
    .in0(n4bit_adder_1_y_4_0), .in1(n4bet_subtructor_1_y_4_0), .in2(not_1_y_4_0), .in3(and_1_p3),
    .in4(or_1_p3), .in5(xor_1_p3), .in6(undriven), .in7(undriven_2), .out(Y_4_0), .en(OP_2_0[0]));  // open: sel
  // Pins of 1 and 4 bits meet at B_3_0
  // Pins of 1 and 3 bits meet at OP_2_0
  // Pins of 1 and 5 bits meet at undriven_2
  // Pins of 1 and 5 bits meet at undriven
endmodule

module COUT4 (
);

  wire clock_1_out, d_ff_1_q, d_ff_1_qn, d_ff_2_q, xor_1_out;

  Clock clock_1 (.out(clock_1_out));
  D_Flip_Flop d_ff_1 (.clk(clock_1_out), .D(d_ff_1_qn), .Q(d_ff_1_q), .Qn(d_ff_1_qn));  // open: preset, en, reset
  D_Flip_Flop d_ff_2 (.clk(clock_1_out), .D(xor_1_out), .Q(d_ff_2_q));  // open: Qn, preset, en, reset
  xor xor_1 (xor_1_out, d_ff_2_q, d_ff_1_q);
endmodule
