// Logisim project dc-06-205713B.circ as structural Verilog: 6 circuits, main circuit main
module main (
  input  [1:0] in_1,
  input  [3:0] in_2,
  output out_3
);

  wire and_1_out, and_2_out, and_3_out, and_4_out, not_1_out, not_2_out;

  not not_1 (not_1_out, in_1[1]);
  not not_2 (not_2_out, in_1[0]);
  and and_1 (and_1_out, not_2_out, not_1_out, in_2[0]);
  and and_2 (and_2_out, in_1[0], not_1_out, in_2[1]);
  and and_3 (and_3_out, not_2_out, in_1[1], in_2[2]);
  and and_4 (and_4_out, in_1[0], in_1[1], in_2[3]);
  or or_1 (out_3, and_1_out, and_2_out, and_3_out, and_4_out);
endmodule

// D
module MUX (
  input  [1:0] S,
  input  [3:0] D,
  output out_3
);

  wire and_1_out, and_2_out, and_3_out, and_4_out, not_1_out, not_2_out;

  not not_1 (not_1_out, S[1]);
  not not_2 (not_2_out, S[0]);
  and and_1 (and_1_out, not_2_out, not_1_out, D[0]);
  and and_2 (and_2_out, S[0], not_1_out, D[1]);
  and and_3 (and_3_out, not_2_out, S[1], D[2]);
  and and_4 (and_4_out, S[0], S[1], D[3]);
  or or_1 (out_3, and_1_out, and_2_out, and_3_out, and_4_out);
endmodule

module DEMUX (
  input  [1:0] S,
  input  D,
  output out_3,
  output out_4,
  output out_5,
  output out_6
);

  wire not_1_out, not_2_out;

  not not_1 (not_1_out, S[1]);
  not not_2 (not_2_out, S[0]);
  and and_1 (out_3, not_2_out, not_1_out, D);
  and and_2 (out_4, S[0], not_1_out, D);
  and and_3 (out_5, not_2_out, S[1], D);
  and and_4 (out_6, S[0], S[1], D);
endmodule

module DECODE (
  input  [1:0] D,
  output out_2,
  output out_3,
  output out_4,
  output out_5
);

  wire not_1_out, not_2_out;

  not not_1 (not_1_out, D[0]);
  not not_2 (not_2_out, D[1]);
  and and_1 (out_2, not_1_out, not_2_out);
  and and_2 (out_3, D[0], not_2_out);
  and and_3 (out_4, not_1_out, D[1]);
  and and_4 (out_5, D[0], D[1]);
endmodule

module ENCODE (
  input  [3:0] in_1,
  output out_2,
  output out_3
);

  wire and_1_out, not_1_out;

  not not_1 (not_1_out, in_1[2]);
  and and_1 (and_1_out, in_1[1], not_1_out);
  or or_1 (out_2, and_1_out, in_1[3]);
  or or_2 (out_3, in_1[2], in_1[3]);
endmodule

module PARITY (
  input  [7:0] in_1,
  output out_2
);

  wire xor_1_out, xor_2_out, xor_3_out, xor_4_out, xor_5_out, xor_6_out, xor_7_out;

  xor xor_1 (xor_1_out, in_1[0], in_1[1]);
  xor xor_2 (xor_2_out, in_1[2], in_1[3]);
  xor xor_3 (xor_3_out, in_1[4], in_1[5]);
  xor xor_4 (xor_4_out, in_1[6], in_1[7]);
  xor xor_5 (xor_5_out, xor_1_out, xor_2_out);
  xor xor_6 (xor_6_out, xor_3_out, xor_4_out);
  not not_1 (out_2, xor_7_out);
  xor xor_7 (xor_7_out, xor_5_out, xor_6_out);
endmodule
