// Logisim project TeC6_Mini.circ as structural Verilog: 15 circuits, main circuit TeC6_Mini
module TeC6_Mini (
);

  wire alu_1_cf, alu_1_sf, alu_1_zf, CLK, MEM_EN, MEM_RW, not_1_out;
  wire [1:0] R_GR, R_XR;
  wire [2:0] FLAG;
  wire [3:0] CS, R_IR;
  wire [7:0] ALU, lm_ctrl_1__00, lm_ctrl_1__01, lm_ctrl_1__02, lm_ctrl_1__03, lm_ctrl_1__04, lm_ctrl_1__05,
       lm_ctrl_1__06, lm_ctrl_1__07, lm_ctrl_1__08, lm_ctrl_1__09, lm_ctrl_1__10, lm_ctrl_1__11,
       lm_ctrl_1__12, lm_ctrl_1__13, lm_ctrl_1__14, lm_ctrl_1__15, lm_ctrl_1__16, lm_ctrl_1__17,
       lm_ctrl_1__18, lm_ctrl_1__19, lm_ctrl_1__20, lm_ctrl_1__21, lm_ctrl_1__22, lm_ctrl_1__23,
       lm_ctrl_1__24, lm_ctrl_1__25, lm_ctrl_1__26, lm_ctrl_1__27, lm_ctrl_1__28, lm_ctrl_1__29,
       lm_ctrl_1__30, lm_ctrl_1__31, MEM_DATA, MEM_DOUT, R_AS1, R_AS2, R_G0, R_G1, R_G2, R_MA, R_PC, R_SB;

  MEM_ADDR mem_addr_1 (
    .CS_3_0(CS), .R_XR_1_0(R_XR), .R_PC_7_0(R_PC), .R_SB_7_0(R_SB), .R_G1_7_0(R_G1), .R_G2_7_0(R_G2),
    .CLK(CLK), .R_MA_7_0(R_MA));
  MEM_DATA mem_data_1 (
    .CS_3_0(CS), .R_GR_3_0(R_GR), .R_G0_7_0(R_G0), .R_G1_7_0(R_G1), .R_G2_7_0(R_G2), .CLK(CLK),
    .MEM_DATA_7_0(MEM_DATA));
  SEC_BYTE sec_byte_1 (.CS_3_0(CS), .MEM_DOUT_7_0(MEM_DOUT), .CLK(CLK), .R_SB_7_0(R_SB));
  CTRL ctrl_1 (.R_IR_3_0(R_IR), .R_XR_1_0(R_XR), .CLK(CLK), .CS_3_0(CS), .MEM_EN(MEM_EN), .MEM_RW(MEM_RW));
  ALU_SRC1 alu_src1_1 (
    .CS_3_0(CS), .R_IR_3_0(R_IR), .R_GR_3_0(R_GR), .R_XR_3_0(R_XR), .R_G0_7_0(R_G0), .R_G1_7_0(R_G1),
    .R_G2_7_0(R_G2), .R_SB_7_0(R_SB), .MEM_DOUT_7_0(MEM_DOUT), .CLK(CLK), .R_AS1_7_0(R_AS1));
  ALU_SRC2 alu_src2_1 (
    .CS_3_0(CS), .R_GR_3_0(R_GR), .R_G0_7_0(R_G0), .R_G1_7_0(R_G1), .R_G2_7_0(R_G2), .CLK(CLK),
    .R_AS2_7_0(R_AS2));
  Clock clock_1 (.out(CLK));
  RAM #(.bus("separate")) ram_1 (
    .addr(R_MA), .din(MEM_DATA), .data(MEM_DOUT), .str(MEM_RW), .sel(MEM_EN), .clk(CLK), .ld(not_1_out));  // open: clr
  not not_1 (not_1_out, MEM_RW);
  // Probe on CS
  // Probe on R_AS1
  // Probe on R_MA
  // Probe on MEM_EN
  // Probe on R_AS2
  DotMatrix #(.matrixcols(32), .matrixrows(8)) dotmatrix_1 (
    .col0(lm_ctrl_1__00), .col1(lm_ctrl_1__01), .col2(lm_ctrl_1__02), .col3(lm_ctrl_1__03),
    .col4(lm_ctrl_1__04), .col5(lm_ctrl_1__05), .col6(lm_ctrl_1__06), .col7(lm_ctrl_1__07),
    .col8(lm_ctrl_1__08), .col9(lm_ctrl_1__09), .col10(lm_ctrl_1__10), .col11(lm_ctrl_1__11),
    .col12(lm_ctrl_1__12), .col13(lm_ctrl_1__13), .col14(lm_ctrl_1__14), .col15(lm_ctrl_1__15),
    .col16(lm_ctrl_1__16), .col17(lm_ctrl_1__17), .col18(lm_ctrl_1__18), .col19(lm_ctrl_1__19),
    .col20(lm_ctrl_1__20), .col21(lm_ctrl_1__21), .col22(lm_ctrl_1__22), .col23(lm_ctrl_1__23),
    .col24(lm_ctrl_1__24), .col25(lm_ctrl_1__25), .col26(lm_ctrl_1__26), .col27(lm_ctrl_1__27),
    .col28(lm_ctrl_1__28), .col29(lm_ctrl_1__29), .col30(lm_ctrl_1__30), .col31(lm_ctrl_1__31));
  LM_CTRL lm_ctrl_1 (
    .CS(CS), .IR(R_IR), .G0(R_G0), .CLK(CLK), ._00(lm_ctrl_1__00), ._01(lm_ctrl_1__01), ._02(lm_ctrl_1__02),
    ._03(lm_ctrl_1__03), ._04(lm_ctrl_1__04), ._05(lm_ctrl_1__05), ._06(lm_ctrl_1__06), ._07(lm_ctrl_1__07),
    ._08(lm_ctrl_1__08), ._09(lm_ctrl_1__09), ._10(lm_ctrl_1__10), ._11(lm_ctrl_1__11), ._12(lm_ctrl_1__12),
    ._13(lm_ctrl_1__13), ._14(lm_ctrl_1__14), ._15(lm_ctrl_1__15), ._16(lm_ctrl_1__16), ._17(lm_ctrl_1__17),
    ._18(lm_ctrl_1__18), ._19(lm_ctrl_1__19), ._20(lm_ctrl_1__20), ._21(lm_ctrl_1__21), ._22(lm_ctrl_1__22),
    ._23(lm_ctrl_1__23), ._24(lm_ctrl_1__24), ._25(lm_ctrl_1__25), ._26(lm_ctrl_1__26), ._27(lm_ctrl_1__27),
    ._28(lm_ctrl_1__28), ._29(lm_ctrl_1__29), ._30(lm_ctrl_1__30), ._31(lm_ctrl_1__31));
  // Probe on R_PC
  // Probe on MEM_RW
  // Probe on FLAG
  // Probe on ALU
  // Probe on R_GR
  // Probe on R_IR
  // Probe on MEM_DATA
  // Probe on R_G0
  // Probe on R_XR
  // Probe on MEM_DOUT
  // Probe on R_G1
  // Probe on R_SB
  // Probe on R_G2
  G0 g0_1 (.CS_3_0(CS), .R_IR_3_0(R_IR), .R_GR_3_0(R_GR), .ALU_7_0(ALU), .CLK(CLK), .R_G0_7_0(R_G0));
  G1 g1_1 (.CS_3_0(CS), .R_IR_3_0(R_IR), .R_GR_3_0(R_GR), .ALU_7_0(ALU), .CLK(CLK), .R_G1_7_0(R_G1));
  G2 g2_1 (.CS_3_0(CS), .R_IR_3_0(R_IR), .R_GR_3_0(R_GR), .ALU_7_0(ALU), .CLK(CLK), .R_G2_7_0(R_G2));
  ALU alu_1 (
    .SEL_3_0(R_IR), .XR_1_0(R_XR), .A_7_0(R_AS1), .B_7_0(R_AS2), .ALU_7_0(ALU), .ZF(alu_1_zf), .CF(alu_1_cf),
    .SF(alu_1_sf));
  PRG_CNT prg_cnt_1 (
    .CS_3_0(CS), .R_GR_1_0(R_GR), .FLAG_2_0(FLAG), .R_XR_1_0(R_XR), .R_SB_7_0(R_SB), .R_G1_7_0(R_G1),
    .R_G2_7_0(R_G2), .CLK(CLK), .R_PC_7_0(R_PC));
  IR_GR_XR ir_gr_xr_1 (
    .CS_3_0(CS), .MEM_DOUT_7_0(MEM_DOUT), .CLK(CLK), .R_IR_3_0(R_IR), .R_GR_1_0(R_GR), .R_XR_1_0(R_XR));
  FLAG flag_1 (.CS_3_0(CS), .ZF(alu_1_zf), .CF(alu_1_cf), .SF(alu_1_sf), .CLK(CLK), .R_FLAG_2_0(FLAG));

  // Notes on the sheet:
  //   CTRL
  //   MAR
  //   MEM_DATA
  //   SEC_BYTE
  //   ALU_SRC1
  //   ALU_SRC2
  //   メインメモリ
  //   クロック
  //   ALU Status
  //   System Status
  //   Memory Status
  //   TeC6_Mini の状態確認欄
  //   8*32 LED Matrix
  //   Register Status
  //   ALU
  //   G0
  //   G1
  //   G2
  //   PC
  //   IR_GR_XR
  //   FLAG
endmodule

module ALU (
  input  [3:0] SEL_3_0,
  input  [1:0] XR_1_0,
  input  [7:0] A_7_0,
  input  [7:0] B_7_0,
  output [7:0] ALU_7_0,
  output ZF,
  output CF,
  output SF
);

  wire adder_1_cout, SH_MSB, subtractor_1_bout;
  wire [7:0] adder_1_out, and_1_out, or_1_out, SH_BD, subtractor_1_out, xor_1_out;

  Adder adder_1 (.a(A_7_0), .b(B_7_0), .out(adder_1_out), .cout(adder_1_cout));  // open: cin
  Subtractor subtractor_1 (.a(B_7_0), .b(A_7_0), .out(subtractor_1_out), .bout(subtractor_1_bout));  // open: bin
  assign and_1_out = A_7_0 & B_7_0;  // AND_Gate and_1, 8 bits wide
  assign or_1_out = A_7_0 | B_7_0;  // OR_Gate or_1, 8 bits wide
  assign xor_1_out = A_7_0 ^ B_7_0;  // XOR_Gate xor_1, 8 bits wide
  Multiplexer #(.select(4), .width(8), .enable("false")) multiplexer_1 (
    .in0({8{1'b0}}), .in1(A_7_0), .in2({8{1'b0}}), .in3(adder_1_out), .in4(subtractor_1_out),
    .in5(subtractor_1_out), .in6(and_1_out), .in7(or_1_out), .in8(xor_1_out), .in9(SH_BD), .in10({8{1'b0}}),
    .in11({8{1'b0}}), .in12({8{1'b0}}), .in13({8{1'b0}}), .in14({8{1'b0}}), .in15({8{1'b0}}), .out(ALU_7_0),
    .sel(SEL_3_0));
  Multiplexer #(.select(4), .enable("false")) multiplexer_2 (
    .in0(1'b0), .in1(1'b0), .in2(1'b0), .in3(adder_1_cout), .in4(subtractor_1_bout), .in5(subtractor_1_bout),
    .in6(1'b0), .in7(1'b0), .in8(1'b0), .in9(SH_MSB), .in10(1'b0), .in11(1'b0), .in12(1'b0), .in13(1'b0),
    .in14(1'b0), .in15(1'b0), .out(CF), .sel(SEL_3_0));
  nor nor_1 (ZF, ALU_7_0[0], ALU_7_0[1], ALU_7_0[2], ALU_7_0[3], ALU_7_0[4], ALU_7_0[5], ALU_7_0[6], ALU_7_0[7]);
  Multiplexer #(.select(2), .width(8), .enable("false")) multiplexer_3 (
    .in0({B_7_0[6:0], 1'b0}), .in1({B_7_0[6:0], B_7_0[7]}), .in2({{2{B_7_0[7]}}, B_7_0[6:1]}),
    .in3({1'b0, B_7_0[7:1]}), .out(SH_BD), .sel(XR_1_0));
  Multiplexer #(.select(2), .enable("false")) multiplexer_4 (
    .in0(B_7_0[7]), .in1(B_7_0[7]), .in2(B_7_0[0]), .in3(B_7_0[0]), .out(SH_MSB), .sel(XR_1_0));

  assign SF = ALU_7_0[7];

  // Other names for the same wires on the sheet: ALU_XR[1:0] = XR_1_0

  // Notes on the sheet:
  //   １ビット左算術シフタ（SHLA）
  //   １ビット左算術シフタ（SHLL）
  //   １ビット右算術シフタ（SHRA）
  //   １ビット右論理シフタ（SHRL）
endmodule

module CTRL (
  input  [3:0] R_IR_3_0,
  input  [1:0] R_XR_1_0,
  input  CLK,
  output [3:0] CS_3_0,
  output MEM_EN,
  output MEM_RW
);

  wire [3:0] multiplexer_1_out, multiplexer_2_out, multiplexer_3_out, multiplexer_4_out;

  Multiplexer #(.select(2), .width(4), .enable("false")) multiplexer_1 (
    .in0(4'b0101), .in1(4'b0101), .in2(4'b0101), .in3(4'b0110), .out(multiplexer_1_out), .sel(R_XR_1_0));
  Multiplexer #(.select(4), .width(4), .enable("false")) multiplexer_2 (
    .in0(4'b0000), .in1(4'b0011), .in2(4'b0011), .in3(4'b0011), .in4(4'b0011), .in5(4'b0011), .in6(4'b0011),
    .in7(4'b0011), .in8(4'b0011), .in9(4'b0110), .in10(4'b0011), .in11(4'b0011), .in12(4'b0011),
    .in13(4'b0011), .in14(4'b0011), .in15(4'b0010), .out(multiplexer_2_out), .sel(R_IR_3_0));
  Multiplexer #(.select(4), .width(4), .enable("false")) multiplexer_3 (
    .in0(multiplexer_1_out), .in1(multiplexer_1_out), .in2(4'b1000), .in3(multiplexer_1_out),
    .in4(multiplexer_1_out), .in5(multiplexer_1_out), .in6(multiplexer_1_out), .in7(multiplexer_1_out),
    .in8(multiplexer_1_out), .in9(multiplexer_1_out), .in10(4'b1010), .in11(multiplexer_1_out),
    .in12(multiplexer_1_out), .in13(multiplexer_1_out), .in14(multiplexer_1_out), .in15(multiplexer_1_out),
    .out(multiplexer_3_out), .sel(R_IR_3_0));
  Multiplexer #(.select(4), .width(4), .enable("false")) multiplexer_4 (
    .in0(4'b0001), .in1(4'b0010), .in2(multiplexer_2_out), .in3(4'b0100), .in4(multiplexer_3_out),
    .in5(4'b0110), .in6(4'b0111), .in7(4'b0000), .in8(4'b1001), .in9(4'b0000), .in10(4'b0000),
    .in11(4'b0000), .in12(4'b0000), .in13(4'b0000), .in14(4'b0000), .in15(4'b0000), .out(multiplexer_4_out),
    .sel(CS_3_0));
  Register #(.width(4)) register_1 (.D(multiplexer_4_out), .Q(CS_3_0), .clk(CLK));  // open: en, clr
  Multiplexer #(.select(4), .enable("false")) multiplexer_5 (
    .in0(1'b0), .in1(1'b1), .in2(1'b0), .in3(1'b0), .in4(1'b1), .in5(1'b0), .in6(1'b1), .in7(1'b0),
    .in8(1'b0), .in9(1'b1), .in10(1'b0), .in11(1'b0), .in12(1'b0), .in13(1'b0), .in14(1'b0), .in15(1'b0),
    .out(MEM_EN), .sel(CS_3_0));
  Multiplexer #(.select(4), .enable("false")) multiplexer_6 (
    .in0(1'b0), .in1(1'b0), .in2(1'b0), .in3(1'b0), .in4(1'b0), .in5(1'b0), .in6(1'b0), .in7(1'b0),
    .in8(1'b0), .in9(1'b1), .in10(1'b0), .in11(1'b0), .in12(1'b0), .in13(1'b0), .in14(1'b0), .in15(1'b0),
    .out(MEM_RW), .sel(CS_3_0));
endmodule

module PRG_CNT (
  input  [3:0] CS_3_0,
  input  [1:0] R_GR_1_0,
  input  [2:0] FLAG_2_0,
  input  [1:0] R_XR_1_0,
  input  [7:0] R_SB_7_0,
  input  [7:0] R_G1_7_0,
  input  [7:0] R_G2_7_0,
  input  CLK,
  output [7:0] R_PC_7_0
);

  wire [7:0] adder_1_out, adder_2_out, adder_3_out, multiplexer_1_out, multiplexer_2_out, multiplexer_3_out,
       multiplexer_4_out, multiplexer_5_out, multiplexer_6_out;

  Adder adder_1 (.a(R_SB_7_0), .b(R_G1_7_0), .out(adder_1_out));  // open: cin, cout
  Adder adder_2 (.a(R_SB_7_0), .b(R_G2_7_0), .out(adder_2_out));  // open: cin, cout
  Multiplexer #(.select(2), .width(8), .enable("false")) multiplexer_1 (
    .in0(R_SB_7_0), .in1(adder_1_out), .in2(adder_2_out), .in3(R_PC_7_0), .out(multiplexer_1_out),
    .sel(R_XR_1_0));
  Multiplexer #(.width(8), .enable("false")) multiplexer_2 (
    .in0(R_PC_7_0), .in1(multiplexer_1_out), .out(multiplexer_2_out), .sel(FLAG_2_0[2]));
  Multiplexer #(.width(8), .enable("false")) multiplexer_3 (
    .in0(R_PC_7_0), .in1(multiplexer_1_out), .out(multiplexer_3_out), .sel(FLAG_2_0[0]));
  Multiplexer #(.width(8), .enable("false")) multiplexer_4 (
    .in0(R_PC_7_0), .in1(multiplexer_1_out), .out(multiplexer_4_out), .sel(FLAG_2_0[1]));
  Adder adder_3 (.a(R_PC_7_0), .b(8'h1), .out(adder_3_out));  // open: cin, cout
  Multiplexer #(.select(2), .width(8), .enable("false")) multiplexer_5 (
    .in0(multiplexer_1_out), .in1(multiplexer_3_out), .in2(multiplexer_4_out), .in3(multiplexer_2_out),
    .out(multiplexer_5_out), .sel(R_GR_1_0));
  Register register_1 (.D(multiplexer_6_out), .Q(R_PC_7_0), .clk(CLK));  // open: en, clr
  Multiplexer #(.select(4), .width(8), .enable("false")) multiplexer_6 (
    .in0(adder_3_out), .in1(R_PC_7_0), .in2(R_PC_7_0), .in3(adder_3_out), .in4(R_PC_7_0), .in5(R_PC_7_0),
    .in6(R_PC_7_0), .in7(R_PC_7_0), .in8(R_PC_7_0), .in9(R_PC_7_0), .in10(multiplexer_5_out),
    .in11(R_PC_7_0), .in12(R_PC_7_0), .in13(R_PC_7_0), .in14(R_PC_7_0), .in15(R_PC_7_0),
    .out(multiplexer_6_out), .sel(CS_3_0));

  // Notes on the sheet:
  //   XR
  //   Carry
  //   Sign
  //   Zero
  //   GR
  //   CS
endmodule

module MEM_ADDR (
  input  [3:0] CS_3_0,
  input  [1:0] R_XR_1_0,
  input  [7:0] R_PC_7_0,
  input  [7:0] R_SB_7_0,
  input  [7:0] R_G1_7_0,
  input  [7:0] R_G2_7_0,
  input  CLK,
  output [7:0] R_MA_7_0
);

  wire [7:0] adder_1_out, adder_2_out, multiplexer_1_out, multiplexer_2_out;

  Adder adder_1 (.a(R_SB_7_0), .b(R_G1_7_0), .out(adder_1_out));  // open: cin, cout
  Adder adder_2 (.a(R_SB_7_0), .b(R_G2_7_0), .out(adder_2_out));  // open: cin, cout
  Multiplexer #(.select(2), .width(8), .enable("false")) multiplexer_1 (
    .in0(R_SB_7_0), .in1(adder_1_out), .in2(adder_2_out), .in3(R_MA_7_0), .out(multiplexer_1_out),
    .sel(R_XR_1_0));
  Multiplexer #(.select(4), .width(8), .enable("false")) multiplexer_2 (
    .in0(R_PC_7_0), .in1(R_MA_7_0), .in2(R_MA_7_0), .in3(R_PC_7_0), .in4(R_MA_7_0), .in5(multiplexer_1_out),
    .in6(R_MA_7_0), .in7(R_MA_7_0), .in8(multiplexer_1_out), .in9(R_MA_7_0), .in10(R_MA_7_0),
    .in11(R_MA_7_0), .in12(R_MA_7_0), .in13(R_MA_7_0), .in14(R_MA_7_0), .in15(R_MA_7_0),
    .out(multiplexer_2_out), .sel(CS_3_0));
  Register register_1 (.D(multiplexer_2_out), .Q(R_MA_7_0), .clk(CLK));  // open: en, clr
endmodule

module IR_GR_XR (
  input  [3:0] CS_3_0,
  input  [7:0] MEM_DOUT_7_0,
  input  CLK,
  output [3:0] R_IR_3_0,
  output [1:0] R_GR_1_0,
  output [1:0] R_XR_1_0
);

  wire [7:0] multiplexer_1_out;

  Multiplexer #(.select(4), .width(8), .enable("false")) multiplexer_1 (
    .in0({R_IR_3_0, R_GR_1_0, R_XR_1_0}), .in1(MEM_DOUT_7_0), .in2({R_IR_3_0, R_GR_1_0, R_XR_1_0}),
    .in3({R_IR_3_0, R_GR_1_0, R_XR_1_0}), .in4({R_IR_3_0, R_GR_1_0, R_XR_1_0}),
    .in5({R_IR_3_0, R_GR_1_0, R_XR_1_0}), .in6({R_IR_3_0, R_GR_1_0, R_XR_1_0}),
    .in7({R_IR_3_0, R_GR_1_0, R_XR_1_0}), .in8({R_IR_3_0, R_GR_1_0, R_XR_1_0}),
    .in9({R_IR_3_0, R_GR_1_0, R_XR_1_0}), .in10({R_IR_3_0, R_GR_1_0, R_XR_1_0}),
    .in11({R_IR_3_0, R_GR_1_0, R_XR_1_0}), .in12({R_IR_3_0, R_GR_1_0, R_XR_1_0}),
    .in13({R_IR_3_0, R_GR_1_0, R_XR_1_0}), .in14({R_IR_3_0, R_GR_1_0, R_XR_1_0}),
    .in15({R_IR_3_0, R_GR_1_0, R_XR_1_0}), .out(multiplexer_1_out), .sel(CS_3_0));
  Register #(.width(4)) register_1 (.D(multiplexer_1_out[7:4]), .Q(R_IR_3_0), .clk(CLK));  // open: en, clr
  Register #(.width(2)) register_2 (.D(multiplexer_1_out[3:2]), .Q(R_GR_1_0), .clk(CLK));  // open: en, clr
  Register #(.width(2)) register_3 (.D(multiplexer_1_out[1:0]), .Q(R_XR_1_0), .clk(CLK));  // open: en, clr

  // Notes on the sheet:
  //   IR
  //   GR
  //   XR
endmodule

module SEC_BYTE (
  input  [3:0] CS_3_0,
  input  [7:0] MEM_DOUT_7_0,
  input  CLK,
  output [7:0] R_SB_7_0
);

  wire [7:0] multiplexer_1_out;

  Multiplexer #(.select(4), .width(8), .enable("false")) multiplexer_1 (
    .in0(R_SB_7_0), .in1(R_SB_7_0), .in2(R_SB_7_0), .in3(R_SB_7_0), .in4(MEM_DOUT_7_0), .in5(R_SB_7_0),
    .in6(R_SB_7_0), .in7(R_SB_7_0), .in8(R_SB_7_0), .in9(R_SB_7_0), .in10(R_SB_7_0), .in11(R_SB_7_0),
    .in12(R_SB_7_0), .in13(R_SB_7_0), .in14(R_SB_7_0), .in15(R_SB_7_0), .out(multiplexer_1_out), .sel(CS_3_0));
  Register register_1 (.D(multiplexer_1_out), .Q(R_SB_7_0), .clk(CLK));  // open: en, clr
endmodule

module ALU_SRC1 (
  input  [3:0] CS_3_0,
  input  [3:0] R_IR_3_0,
  input  [1:0] R_GR_3_0,
  input  [1:0] R_XR_3_0,
  input  [7:0] R_G0_7_0,
  input  [7:0] R_G1_7_0,
  input  [7:0] R_G2_7_0,
  input  [7:0] R_SB_7_0,
  input  [7:0] MEM_DOUT_7_0,
  input  CLK,
  output [7:0] R_AS1_7_0
);

  wire [7:0] multiplexer_1_out, multiplexer_2_out, multiplexer_3_out, multiplexer_4_out;

  Multiplexer #(.select(2), .width(8), .enable("false")) multiplexer_1 (
    .in0(R_G0_7_0), .in1(R_G1_7_0), .in2(R_G2_7_0), .in3(R_AS1_7_0), .out(multiplexer_1_out), .sel(R_GR_3_0));
  Multiplexer #(.select(2), .width(8), .enable("false")) multiplexer_2 (
    .in0(MEM_DOUT_7_0), .in1(MEM_DOUT_7_0), .in2(MEM_DOUT_7_0), .in3(R_SB_7_0), .out(multiplexer_2_out),
    .sel(R_XR_3_0));
  Multiplexer #(.select(4), .width(8), .enable("false")) multiplexer_3 (
    .in0(multiplexer_2_out), .in1(multiplexer_2_out), .in2(multiplexer_2_out), .in3(multiplexer_2_out),
    .in4(multiplexer_2_out), .in5(multiplexer_2_out), .in6(multiplexer_2_out), .in7(multiplexer_2_out),
    .in8(multiplexer_2_out), .in9(multiplexer_1_out), .in10(multiplexer_2_out), .in11(multiplexer_2_out),
    .in12(multiplexer_2_out), .in13(multiplexer_2_out), .in14(multiplexer_2_out), .in15(multiplexer_2_out),
    .out(multiplexer_3_out), .sel(R_IR_3_0));
  Multiplexer #(.select(4), .width(8), .enable("false")) multiplexer_4 (
    .in0(R_AS1_7_0), .in1(R_AS1_7_0), .in2(R_AS1_7_0), .in3(R_AS1_7_0), .in4(R_AS1_7_0), .in5(R_AS1_7_0),
    .in6(multiplexer_3_out), .in7(R_AS1_7_0), .in8(R_AS1_7_0), .in9(R_AS1_7_0), .in10(R_AS1_7_0),
    .in11(R_AS1_7_0), .in12(R_AS1_7_0), .in13(R_AS1_7_0), .in14(R_AS1_7_0), .in15(R_AS1_7_0),
    .out(multiplexer_4_out), .sel(CS_3_0));
  Register register_1 (.D(multiplexer_4_out), .Q(R_AS1_7_0), .clk(CLK));  // open: en, clr
endmodule

module ALU_SRC2 (
  input  [3:0] CS_3_0,
  input  [1:0] R_GR_3_0,
  input  [7:0] R_G0_7_0,
  input  [7:0] R_G1_7_0,
  input  [7:0] R_G2_7_0,
  input  CLK,
  output [7:0] R_AS2_7_0
);

  wire [7:0] multiplexer_1_out, multiplexer_2_out;

  Multiplexer #(.select(2), .width(8), .enable("false")) multiplexer_1 (
    .in0(R_G0_7_0), .in1(R_G1_7_0), .in2(R_G2_7_0), .in3(R_AS2_7_0), .out(multiplexer_1_out), .sel(R_GR_3_0));
  Multiplexer #(.select(4), .width(8), .enable("false")) multiplexer_2 (
    .in0(R_AS2_7_0), .in1(R_AS2_7_0), .in2(R_AS2_7_0), .in3(R_AS2_7_0), .in4(R_AS2_7_0), .in5(R_AS2_7_0),
    .in6(multiplexer_1_out), .in7(R_AS2_7_0), .in8(R_AS2_7_0), .in9(R_AS2_7_0), .in10(R_AS2_7_0),
    .in11(R_AS2_7_0), .in12(R_AS2_7_0), .in13(R_AS2_7_0), .in14(R_AS2_7_0), .in15(R_AS2_7_0),
    .out(multiplexer_2_out), .sel(CS_3_0));
  Register register_1 (.D(multiplexer_2_out), .Q(R_AS2_7_0), .clk(CLK));  // open: en, clr
endmodule

module FLAG (
  input  [3:0] CS_3_0,
  input  ZF,
  input  CF,
  input  SF,
  input  CLK,
  output [2:0] R_FLAG_2_0
);

  wire multiplexer_1_out, multiplexer_2_out, multiplexer_3_out;

  Multiplexer #(.select(4), .enable("false")) multiplexer_1 (
    .in0(R_FLAG_2_0[2]), .in1(R_FLAG_2_0[2]), .in2(R_FLAG_2_0[2]), .in3(R_FLAG_2_0[2]), .in4(R_FLAG_2_0[2]),
    .in5(R_FLAG_2_0[2]), .in6(R_FLAG_2_0[2]), .in7(SF), .in8(R_FLAG_2_0[2]), .in9(R_FLAG_2_0[2]),
    .in10(R_FLAG_2_0[2]), .in11(R_FLAG_2_0[2]), .in12(R_FLAG_2_0[2]), .in13(R_FLAG_2_0[2]),
    .in14(R_FLAG_2_0[2]), .in15(R_FLAG_2_0[2]), .out(multiplexer_1_out), .sel(CS_3_0));
  Multiplexer #(.select(4), .enable("false")) multiplexer_2 (
    .in0(R_FLAG_2_0[1]), .in1(R_FLAG_2_0[1]), .in2(R_FLAG_2_0[1]), .in3(R_FLAG_2_0[1]), .in4(R_FLAG_2_0[1]),
    .in5(R_FLAG_2_0[1]), .in6(R_FLAG_2_0[1]), .in7(CF), .in8(R_FLAG_2_0[1]), .in9(R_FLAG_2_0[1]),
    .in10(R_FLAG_2_0[1]), .in11(R_FLAG_2_0[1]), .in12(R_FLAG_2_0[1]), .in13(R_FLAG_2_0[1]),
    .in14(R_FLAG_2_0[1]), .in15(R_FLAG_2_0[1]), .out(multiplexer_2_out), .sel(CS_3_0));
  Multiplexer #(.select(4), .enable("false")) multiplexer_3 (
    .in0(R_FLAG_2_0[0]), .in1(R_FLAG_2_0[0]), .in2(R_FLAG_2_0[0]), .in3(R_FLAG_2_0[0]), .in4(R_FLAG_2_0[0]),
    .in5(R_FLAG_2_0[0]), .in6(R_FLAG_2_0[0]), .in7(ZF), .in8(R_FLAG_2_0[0]), .in9(R_FLAG_2_0[0]),
    .in10(R_FLAG_2_0[0]), .in11(R_FLAG_2_0[0]), .in12(R_FLAG_2_0[0]), .in13(R_FLAG_2_0[0]),
    .in14(R_FLAG_2_0[0]), .in15(R_FLAG_2_0[0]), .out(multiplexer_3_out), .sel(CS_3_0));
  Register #(.width(1)) register_1 (.D(multiplexer_3_out), .Q(R_FLAG_2_0[0]), .clk(CLK));  // open: en, clr
  Register #(.width(1)) register_2 (.D(multiplexer_2_out), .Q(R_FLAG_2_0[1]), .clk(CLK));  // open: en, clr
  Register #(.width(1)) register_3 (.D(multiplexer_1_out), .Q(R_FLAG_2_0[2]), .clk(CLK));  // open: en, clr
endmodule

module G0 (
  input  [3:0] CS_3_0,
  input  [3:0] R_IR_3_0,
  input  [1:0] R_GR_3_0,
  input  [7:0] ALU_7_0,
  input  CLK,
  output [7:0] R_G0_7_0
);

  wire [7:0] multiplexer_1_out, multiplexer_2_out, multiplexer_3_out;

  Multiplexer #(.select(2), .width(8), .enable("false")) multiplexer_1 (
    .in0(ALU_7_0), .in1(R_G0_7_0), .in2(R_G0_7_0), .in3(R_G0_7_0), .out(multiplexer_1_out), .sel(R_GR_3_0));
  Multiplexer #(.select(4), .width(8), .enable("false")) multiplexer_2 (
    .in0(multiplexer_1_out), .in1(multiplexer_1_out), .in2(multiplexer_1_out), .in3(multiplexer_1_out),
    .in4(multiplexer_1_out), .in5(R_G0_7_0), .in6(multiplexer_1_out), .in7(multiplexer_1_out),
    .in8(multiplexer_1_out), .in9(multiplexer_1_out), .in10(multiplexer_1_out), .in11(multiplexer_1_out),
    .in12(multiplexer_1_out), .in13(multiplexer_1_out), .in14(multiplexer_1_out), .in15(multiplexer_1_out),
    .out(multiplexer_2_out), .sel(R_IR_3_0));
  Multiplexer #(.select(4), .width(8), .enable("false")) multiplexer_3 (
    .in0(R_G0_7_0), .in1(R_G0_7_0), .in2(R_G0_7_0), .in3(R_G0_7_0), .in4(R_G0_7_0), .in5(R_G0_7_0),
    .in6(R_G0_7_0), .in7(multiplexer_2_out), .in8(R_G0_7_0), .in9(R_G0_7_0), .in10(R_G0_7_0),
    .in11(R_G0_7_0), .in12(R_G0_7_0), .in13(R_G0_7_0), .in14(R_G0_7_0), .in15(R_G0_7_0),
    .out(multiplexer_3_out), .sel(CS_3_0));
  Register register_1 (.D(multiplexer_3_out), .Q(R_G0_7_0), .clk(CLK));  // open: en, clr
endmodule

module G1 (
  input  [3:0] CS_3_0,
  input  [3:0] R_IR_3_0,
  input  [1:0] R_GR_3_0,
  input  [7:0] ALU_7_0,
  input  CLK,
  output [7:0] R_G1_7_0
);

  wire [7:0] multiplexer_1_out, multiplexer_2_out, multiplexer_3_out;

  Multiplexer #(.select(2), .width(8), .enable("false")) multiplexer_1 (
    .in0(R_G1_7_0), .in1(ALU_7_0), .in2(R_G1_7_0), .in3(R_G1_7_0), .out(multiplexer_1_out), .sel(R_GR_3_0));
  Multiplexer #(.select(4), .width(8), .enable("false")) multiplexer_2 (
    .in0(multiplexer_1_out), .in1(multiplexer_1_out), .in2(multiplexer_1_out), .in3(multiplexer_1_out),
    .in4(multiplexer_1_out), .in5(R_G1_7_0), .in6(multiplexer_1_out), .in7(multiplexer_1_out),
    .in8(multiplexer_1_out), .in9(multiplexer_1_out), .in10(multiplexer_1_out), .in11(multiplexer_1_out),
    .in12(multiplexer_1_out), .in13(multiplexer_1_out), .in14(multiplexer_1_out), .in15(multiplexer_1_out),
    .out(multiplexer_2_out), .sel(R_IR_3_0));
  Multiplexer #(.select(4), .width(8), .enable("false")) multiplexer_3 (
    .in0(R_G1_7_0), .in1(R_G1_7_0), .in2(R_G1_7_0), .in3(R_G1_7_0), .in4(R_G1_7_0), .in5(R_G1_7_0),
    .in6(R_G1_7_0), .in7(multiplexer_2_out), .in8(R_G1_7_0), .in9(R_G1_7_0), .in10(R_G1_7_0),
    .in11(R_G1_7_0), .in12(R_G1_7_0), .in13(R_G1_7_0), .in14(R_G1_7_0), .in15(R_G1_7_0),
    .out(multiplexer_3_out), .sel(CS_3_0));
  Register register_1 (.D(multiplexer_3_out), .Q(R_G1_7_0), .clk(CLK));  // open: en, clr
endmodule

module G2 (
  input  [3:0] CS_3_0,
  input  [3:0] R_IR_3_0,
  input  [1:0] R_GR_3_0,
  input  [7:0] ALU_7_0,
  input  CLK,
  output [7:0] R_G2_7_0
);

  wire [7:0] multiplexer_1_out, multiplexer_2_out, multiplexer_3_out;

  Multiplexer #(.select(2), .width(8), .enable("false")) multiplexer_1 (
    .in0(R_G2_7_0), .in1(R_G2_7_0), .in2(ALU_7_0), .in3(R_G2_7_0), .out(multiplexer_1_out), .sel(R_GR_3_0));
  Multiplexer #(.select(4), .width(8), .enable("false")) multiplexer_2 (
    .in0(multiplexer_1_out), .in1(multiplexer_1_out), .in2(multiplexer_1_out), .in3(multiplexer_1_out),
    .in4(multiplexer_1_out), .in5(R_G2_7_0), .in6(multiplexer_1_out), .in7(multiplexer_1_out),
    .in8(multiplexer_1_out), .in9(multiplexer_1_out), .in10(multiplexer_1_out), .in11(multiplexer_1_out),
    .in12(multiplexer_1_out), .in13(multiplexer_1_out), .in14(multiplexer_1_out), .in15(multiplexer_1_out),
    .out(multiplexer_2_out), .sel(R_IR_3_0));
  Multiplexer #(.select(4), .width(8), .enable("false")) multiplexer_3 (
    .in0(R_G2_7_0), .in1(R_G2_7_0), .in2(R_G2_7_0), .in3(R_G2_7_0), .in4(R_G2_7_0), .in5(R_G2_7_0),
    .in6(R_G2_7_0), .in7(multiplexer_2_out), .in8(R_G2_7_0), .in9(R_G2_7_0), .in10(R_G2_7_0),
    .in11(R_G2_7_0), .in12(R_G2_7_0), .in13(R_G2_7_0), .in14(R_G2_7_0), .in15(R_G2_7_0),
    .out(multiplexer_3_out), .sel(CS_3_0));
  Register register_1 (.D(multiplexer_3_out), .Q(R_G2_7_0), .clk(CLK));  // open: en, clr
endmodule

module MEM_DATA (
  input  [3:0] CS_3_0,
  input  [1:0] R_GR_3_0,
  input  [7:0] R_G0_7_0,
  input  [7:0] R_G1_7_0,
  input  [7:0] R_G2_7_0,
  input  CLK,
  output [7:0] MEM_DATA_7_0
);

  wire [7:0] multiplexer_1_out, multiplexer_2_out;

  Multiplexer #(.select(2), .width(8), .enable("false")) multiplexer_1 (
    .in0(R_G0_7_0), .in1(R_G1_7_0), .in2(R_G2_7_0), .in3(MEM_DATA_7_0), .out(multiplexer_1_out),
    .sel(R_GR_3_0));
  Multiplexer #(.select(4), .width(8), .enable("false")) multiplexer_2 (
    .in0(MEM_DATA_7_0), .in1(MEM_DATA_7_0), .in2(MEM_DATA_7_0), .in3(MEM_DATA_7_0), .in4(MEM_DATA_7_0),
    .in5(MEM_DATA_7_0), .in6(MEM_DATA_7_0), .in7(MEM_DATA_7_0), .in8(multiplexer_1_out), .in9(MEM_DATA_7_0),
    .in10(MEM_DATA_7_0), .in11(MEM_DATA_7_0), .in12(MEM_DATA_7_0), .in13(MEM_DATA_7_0), .in14(MEM_DATA_7_0),
    .in15(MEM_DATA_7_0), .out(multiplexer_2_out), .sel(CS_3_0));
  Register register_1 (.D(multiplexer_2_out), .Q(MEM_DATA_7_0), .clk(CLK));  // open: en, clr
endmodule

module LM_CTRL (
  input  [3:0] CS,
  input  [3:0] IR,
  input  [7:0] G0,
  input  CLK,
  output [7:0] _00,
  output [7:0] _01,
  output [7:0] _02,
  output [7:0] _03,
  output [7:0] _04,
  output [7:0] _05,
  output [7:0] _06,
  output [7:0] _07,
  output [7:0] _08,
  output [7:0] _09,
  output [7:0] _10,
  output [7:0] _11,
  output [7:0] _12,
  output [7:0] _13,
  output [7:0] _14,
  output [7:0] _15,
  output [7:0] _16,
  output [7:0] _17,
  output [7:0] _18,
  output [7:0] _19,
  output [7:0] _20,
  output [7:0] _21,
  output [7:0] _22,
  output [7:0] _23,
  output [7:0] _24,
  output [7:0] _25,
  output [7:0] _26,
  output [7:0] _27,
  output [7:0] _28,
  output [7:0] _29,
  output [7:0] _30,
  output [7:0] _31
);

  wire nor_1_out, not_1_out;

  not not_1 (not_1_out, CS[1]);
  nor nor_1 (nor_1_out, CS[0], not_1_out, CS[2], CS[3], IR[0], IR[1], IR[2], IR[3]);
  Shift_Register #(.width(8), .length(32)) shift_register_1 (
    .shift(nor_1_out), .in(G0), .clk(CLK), .q0(_31), .q1(_30), .q2(_29), .q3(_28), .q4(_27), .q5(_26),
    .q6(_25), .q7(_24), .q8(_23), .q9(_22), .q10(_21), .q11(_20), .q12(_19), .q13(_18), .q14(_17), .q15(_16),
    .q16(_15), .q17(_14), .q18(_13), .q19(_12), .q20(_11), .q21(_10), .q22(_09), .q23(_08), .q24(_07),
    .q25(_06), .q26(_05), .q27(_04), .q28(_03), .q29(_02), .q30(_01), .q31(_00));  // open: out, load, clr, d0, d1, d2, d3, d4, d5, d6, d7, d8, d9, d10, d11, d12, d13, d14, d15, d16, d17, d18, d19, d20, d21, d22, d23, d24, d25, d26, d27, d28, d29, d30, d31
endmodule
