// Logisim project dc-06-205728A.circ as structural Verilog: 1 circuit, main circuit main
module main (
);

  wire and_1_out, and_2_out, and_3_out, and_4_out, not_1_out, not_2_out, undriven, undriven_2, undriven_3,
       undriven_4, undriven_5, undriven_6;

  not not_1 (not_1_out, undriven_5);
  not not_2 (not_2_out, undriven_6);
  and and_1 (and_1_out, undriven, not_1_out, not_2_out);
  and and_2 (and_2_out, undriven_2, not_1_out, not_2_out);
  and and_3 (and_3_out, undriven_3, not_1_out, not_2_out);
  and and_4 (and_4_out, undriven_4, not_1_out, not_2_out);
  // OR_Gate or_1 has open pins: in0=and_1_out, in1=and_2_out, in2=and_3_out, in3=and_4_out, out=open

  // Notes on the sheet:
  //   4-bit multiplexer
  //   A
  //   D0
  //   D1
  //   D2
  //   D3
  //   B
endmodule
