// Logisim project dc-10-205728A.circ as structural Verilog: 4 circuits, main circuit ALU
module ALU (
  input  [3:0] A,
  input  [3:0] B,
  input  [3:0] opencode,
  output Z,
  output N,
  output V,
  output C,
  output [3:0] Y
);

  wire [3:0] au_1_y, lu_1_y, multiplexer_1_out, multiplexer_2_out, not_1_out, not_2_out;

  assign not_1_out = ~A;  // NOT_Gate not_1, 4 bits wide
  assign not_2_out = ~B;  // NOT_Gate not_2, 4 bits wide
  Multiplexer #(.width(4), .disabled(0), .enable("false")) multiplexer_1 (
    .in0(A), .in1(not_1_out), .out(multiplexer_1_out), .sel(opencode[0]));
  Multiplexer #(.width(4), .disabled(0), .enable("false")) multiplexer_2 (
    .in0(B), .in1(not_2_out), .out(multiplexer_2_out), .sel(opencode[1]));
  AU au_1 (.cin(opencode[2]), .A(multiplexer_1_out), .B(multiplexer_2_out), .Y(au_1_y), .overflow(V), .cout(C));
  LU lu_1 (.A(A), .B(multiplexer_2_out), .f2(opencode[2]), .f0(opencode[0]), .Y(lu_1_y));
  Multiplexer #(.width(4), .disabled(0), .enable("false")) multiplexer_3 (
    .in0(au_1_y), .in1(lu_1_y), .out({N, Y[2:0]}), .sel(opencode[3]));
  or or_1 (Z, Y[0], Y[1], Y[2], N);

  assign Y[3] = N;

  // Notes on the sheet:
  //   AU
  //   LU
endmodule

module AU (
  input  cin,
  input  [3:0] A,
  input  [3:0] B,
  output [3:0] Y,
  output overflow,
  output cout
);

  wire adder_1_cout, adder_2_cout, adder_3_cout;

  Adder #(.width(1)) adder_1 (.a(A[0]), .b(B[0]), .out(Y[0]), .cin(cin), .cout(adder_1_cout));
  Adder #(.width(1)) adder_2 (.a(A[1]), .b(B[1]), .out(Y[1]), .cin(adder_1_cout), .cout(adder_2_cout));
  Adder #(.width(1)) adder_3 (.a(A[2]), .b(B[2]), .out(Y[2]), .cin(adder_2_cout), .cout(adder_3_cout));
  Adder #(.width(1)) adder_4 (.a(A[3]), .b(B[3]), .out(Y[3]), .cin(adder_3_cout), .cout(cout));
  xor xor_1 (overflow, adder_3_cout, cout);
endmodule

module LU (
  input  [3:0] A,
  input  [3:0] B,
  input  f2,
  input  f0,
  output [3:0] Y
);

  wire [3:0] and_1_out, or_1_out, xor_1_out;

  assign and_1_out = A & B;  // AND_Gate and_1, 4 bits wide
  assign or_1_out = A | B;  // OR_Gate or_1, 4 bits wide
  assign xor_1_out = A ^ B;  // XOR_Gate xor_1, 4 bits wide
  Multiplexer #(.select(2), .width(4), .disabled(0), .enable("false")) multiplexer_1 (
    .in0(and_1_out), .in1(or_1_out), .in2(xor_1_out), .in3(B), .out(Y), .sel({f2, f0}));
endmodule

module COUNT4 (
);

  wire clock_1_out, d_ff_1_q, d_ff_1_qn, d_ff_2_q, xor_1_out;

  Clock clock_1 (.out(clock_1_out));
  D_Flip_Flop d_ff_1 (.clk(clock_1_out), .D(d_ff_1_qn), .Q(d_ff_1_q), .Qn(d_ff_1_qn));  // open: preset, en, reset
  D_Flip_Flop d_ff_2 (.clk(clock_1_out), .D(xor_1_out), .Q(d_ff_2_q));  // open: Qn, preset, en, reset
  xor xor_1 (xor_1_out, d_ff_2_q, d_ff_1_q);
endmodule
