// Logisim project dc-12-205728A.circ as structural Verilog
module _2_bit_counter (
);

  wire clock_1_out, d_ff_1_q, d_ff_1_qn, d_ff_2_q, xor_1_out;

  Clock clock_1 (.out(clock_1_out));
  D_Flip_Flop d_ff_1 (.clk(clock_1_out), .D(d_ff_1_qn), .Q(d_ff_1_q), .Qn(d_ff_1_qn));  // open: preset, en, reset
  D_Flip_Flop d_ff_2 (.clk(clock_1_out), .D(xor_1_out), .Q(d_ff_2_q));  // open: Qn, preset, en, reset
  xor xor_1 (xor_1_out, d_ff_2_q, d_ff_1_q);
endmodule

module _3_bit_counter (
);

  wire and_1_out, clock_1_out, j_k_ff_1_q, j_k_ff_2_q, j_k_ff_3_q, undriven;

  Clock clock_1 (.out(clock_1_out));
  J_K_Flip_Flop j_k_ff_1 (
    .J(undriven), .clk(clock_1_out), .K(undriven), .Q(j_k_ff_1_q));  // open: Qn, preset, en, reset
  J_K_Flip_Flop j_k_ff_2 (
    .J(j_k_ff_1_q), .clk(clock_1_out), .K(j_k_ff_1_q), .Q(j_k_ff_2_q));  // open: Qn, preset, en, reset
  and and_1 (and_1_out, j_k_ff_1_q, j_k_ff_2_q);
  J_K_Flip_Flop j_k_ff_3 (
    .J(and_1_out), .clk(clock_1_out), .K(and_1_out), .Q(j_k_ff_3_q));  // open: Qn, preset, en, reset

  // Notes on the sheet:
  //   1
  //   FF0
  //   Q0
  //   Q1
  //   FF1
  //   FF2
  //   Q2
endmodule

module _5_ary_counter (
);

  wire and_1_out, and_2_out, clock_1_out, d_ff_1_q, d_ff_1_qn, d_ff_2_q, d_ff_3_q, d_ff_3_qn, xor_1_out;

  Clock clock_1 (.out(clock_1_out));
  and and_1 (and_1_out, d_ff_3_qn, d_ff_1_qn);
  D_Flip_Flop d_ff_1 (.clk(clock_1_out), .D(and_1_out), .Q(d_ff_1_q), .Qn(d_ff_1_qn));  // open: preset, en, reset
  xor xor_1 (xor_1_out, d_ff_2_q, d_ff_1_q);
  D_Flip_Flop d_ff_2 (.clk(clock_1_out), .D(xor_1_out), .Q(d_ff_2_q));  // open: Qn, preset, en, reset
  and and_2 (and_2_out, d_ff_1_q, d_ff_2_q);
  D_Flip_Flop d_ff_3 (.clk(clock_1_out), .D(and_2_out), .Q(d_ff_3_q), .Qn(d_ff_3_qn));  // open: preset, en, reset

  // Notes on the sheet:
  //   Q0
  //   Q1
  //   Q2
endmodule

module _16_ary_counter (
);

  wire and_1_out, and_2_out, j_k_ff_1_q, j_k_ff_2_q, j_k_ff_3_q, j_k_ff_4_q, undriven, undriven_2, undriven_3;

  and and_1 (and_1_out, j_k_ff_2_q, j_k_ff_3_q, j_k_ff_4_q);
  and and_2 (and_2_out, j_k_ff_3_q, j_k_ff_4_q);
  J_K_Flip_Flop j_k_ff_1 (
    .J(and_1_out), .clk(undriven_2), .K(and_1_out), .Q(j_k_ff_1_q), .en(undriven_3));  // open: Qn, preset, reset
  J_K_Flip_Flop j_k_ff_2 (
    .J(and_2_out), .clk(undriven_2), .K(and_2_out), .Q(j_k_ff_2_q), .en(undriven_3));  // open: Qn, preset, reset
  J_K_Flip_Flop j_k_ff_3 (
    .J(j_k_ff_4_q), .clk(undriven_2), .K(j_k_ff_4_q), .Q(j_k_ff_3_q), .en(undriven_3));  // open: Qn, preset, reset
  J_K_Flip_Flop j_k_ff_4 (
    .J(undriven), .clk(undriven_2), .K(undriven), .Q(j_k_ff_4_q), .en(undriven_3));  // open: Qn, preset, reset

  // Notes on the sheet:
  //   Q3
  //   Q2
  //   Q1
  //   Q0
endmodule

module _10_ary_counter (
);

  wire and_1_out, and_2_out, and_3_out, and_4_out, j_k_ff_1_q, j_k_ff_1_qn, j_k_ff_2_q, j_k_ff_3_q,
       j_k_ff_4_q, or_1_out, undriven, undriven_2, undriven_3;

  and and_1 (and_1_out, j_k_ff_1_q, j_k_ff_4_q);
  and and_2 (and_2_out, j_k_ff_2_q, j_k_ff_3_q, j_k_ff_4_q);
  or or_1 (or_1_out, and_1_out, and_2_out);
  and and_3 (and_3_out, j_k_ff_3_q, j_k_ff_4_q);
  and and_4 (and_4_out, j_k_ff_1_qn, j_k_ff_4_q);
  J_K_Flip_Flop j_k_ff_1 (
    .J(or_1_out), .clk(undriven), .K(or_1_out), .Q(j_k_ff_1_q), .Qn(j_k_ff_1_qn), .en(undriven_3));  // open: preset, reset
  J_K_Flip_Flop j_k_ff_2 (
    .J(and_3_out), .clk(undriven), .K(and_3_out), .Q(j_k_ff_2_q), .en(undriven_3));  // open: Qn, preset, reset
  J_K_Flip_Flop j_k_ff_3 (
    .J(and_4_out), .clk(undriven), .K(and_4_out), .Q(j_k_ff_3_q), .en(undriven_3));  // open: Qn, preset, reset
  J_K_Flip_Flop j_k_ff_4 (
    .J(undriven_2), .clk(undriven), .K(undriven_2), .Q(j_k_ff_4_q), .en(undriven_3));  // open: Qn, preset, reset

  // Notes on the sheet:
  //   Q3
  //   Q2
  //   Q1
  //   Q0
endmodule
